# Fritzing sketch GROUP SYNTH (saved by Fritzing 0.9.9b)
breadboards: 1

parts:
  Argon1 = Particle Argon
  M1 = BMP280
  Grove_Ultrasonic_Ranger1 = Grove Ultrasonic Ranger
  Grove_Ultrasonic_Ranger2 = Grove Ultrasonic Ranger
  Grove_Ultrasonic_Ranger3 = Grove Ultrasonic Ranger
  Grove_Ultrasonic_Ranger4 = Grove Ultrasonic Ranger
  Grove_Ultrasonic_Ranger5 = Grove Ultrasonic Ranger
  Grove_Ultrasonic_Ranger6 = Grove Ultrasonic Ranger
  Grove_Ultrasonic_Ranger7 = Grove Ultrasonic Ranger
  J1 = Camdenboss CTB0158-3 [part_number=CTB0158-3 package=THT]
  DFRobot_DFPlayer_Mini2 = DFRobot DFPlayer Mini [part_number=DFR0299]
  R1 = Resistor [tolerance=±5% power=0.25 resistance=220 package=THT]
  SP1 = SPEAKER [package=pcb_mount_speaker]
  Neopixel1 = Adafruit RBG Smart Neopixel [package="DIP (Dual Inline) [THT]"]
  Neopixel2 = Adafruit RBG Smart Neopixel [package="DIP (Dual Inline) [THT]"]
  Neopixel3 = Adafruit RBG Smart Neopixel [package="DIP (Dual Inline) [THT]"]
  Neopixel4 = Adafruit RBG Smart Neopixel [package="DIP (Dual Inline) [THT]"]
  Neopixel5 = Adafruit RBG Smart Neopixel [package="DIP (Dual Inline) [THT]"]
  Neopixel6 = Adafruit RBG Smart Neopixel [package="DIP (Dual Inline) [THT]"]
  Neopixel7 = Adafruit RBG Smart Neopixel [package="DIP (Dual Inline) [THT]"]

nets:
  VCC: Argon1.3.3V, M1.VIN, Grove_Ultrasonic_Ranger1.VCC, Grove_Ultrasonic_Ranger2.VCC, Grove_Ultrasonic_Ranger3.VCC, Grove_Ultrasonic_Ranger4.VCC, Grove_Ultrasonic_Ranger5.VCC, Grove_Ultrasonic_Ranger6.VCC, Grove_Ultrasonic_Ranger7.VCC, DFRobot_DFPlayer_Mini2.VCC
  GND: Argon1.GND, M1.GND, Grove_Ultrasonic_Ranger1.GND, Grove_Ultrasonic_Ranger2.GND, Grove_Ultrasonic_Ranger3.GND, Grove_Ultrasonic_Ranger4.GND, Grove_Ultrasonic_Ranger5.GND, Grove_Ultrasonic_Ranger6.GND, Grove_Ultrasonic_Ranger7.GND, J1.pin3, DFRobot_DFPlayer_Mini2.GND-1, DFRobot_DFPlayer_Mini2.GND-2, Neopixel1.G, Neopixel2.G, Neopixel3.G, Neopixel4.G, Neopixel5.G, Neopixel6.G, Neopixel7.G
  N1: Argon1.A0, Grove_Ultrasonic_Ranger7.SIG
  N2: Argon1.A1, Grove_Ultrasonic_Ranger1.SIG
  N3: Argon1.A2, Grove_Ultrasonic_Ranger6.SIG
  N4: Argon1.A3, Grove_Ultrasonic_Ranger2.SIG
  N5: Argon1.A4, Grove_Ultrasonic_Ranger5.SIG
  N6: Argon1.A5, Grove_Ultrasonic_Ranger3.SIG
  N7: Argon1.SCK, Grove_Ultrasonic_Ranger4.SIG
  N8: Argon1.RX, R1.Pin_0
  N9: Argon1.TX, DFRobot_DFPlayer_Mini2.TX
  N10: Argon1.SDA, M1.SDA
  N11: Argon1.SCL, M1.SCL
  N12: Argon1.D8, Neopixel1.In
  N13: J1.pin1, Neopixel1.+, Neopixel2.+, Neopixel3.+, Neopixel4.+, Neopixel5.+, Neopixel6.+, Neopixel7.+
  N14: DFRobot_DFPlayer_Mini2.RX, R1.Pin_1
  N15: DFRobot_DFPlayer_Mini2.SPK_1, SP1.+
  N16: DFRobot_DFPlayer_Mini2.SPK_2, SP1.-
  N17: Neopixel1.O, Neopixel2.In
  N18: Neopixel2.O, Neopixel3.In
  N19: Neopixel3.O, Neopixel4.In
  N20: Neopixel4.O, Neopixel5.In
  N21: Neopixel5.O, Neopixel6.In
  N22: Neopixel6.O, Neopixel7.In

custom parts:
  Particle Argon: The Argon is a powerful Wi-Fi enabled development board that can act as either a standalone Wi-Fi endpoint or Wi-Fi enabled gateway for Particle Mesh networks. It is based on the Nordic nRF52840 and has built-in battery charging circuitry so it’s easy to connect a Li-Po and deploy your local network in minutes. The Argon is great for connecting existing projects to the Particle Device Cloud or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
  BMP280: Temperature Humidity Barometric presure Sensor, I2C
  Grove Ultrasonic Ranger: Ultrasonic Ranger, Grove connector.
